# Fritzing sketch HumidityTemperatureGauge (saved by Fritzing 0.9.10b)
breadboards: 1

parts:
  Part1 = Arduino Uno (Rev3)-TopMount
  Part2 = Adafruit BME680
  Power_plug1 = Power plug
  JACK1 = 2.1mm Barrel Jack with Terminal Block

nets:
  N1: Part1.D9_PWM, Part2.SDO/ADR
  N2: Part1.D10_PWM/SS, Part2.SCK/SCL
  5V: Part1.5V, Part2.VIN
  GND: Part1.GND, Part2.GND
  N3: Power_plug1.GND, JACK1.NEG
  N4: Power_plug1.VCC, JACK1.POS

custom parts:
  Arduino Uno (Rev3)-TopMount: Arduino Uno (Rev3) for Top PCB Mount. The PCB view of the Arduino Uno (Rev3) in Arduino Bin flipped upside down with the text flipped back so as to be readable. Other views haven't changed Protruding component position is outlined to provide indication of part contact. Number in component outline is mm of protrusion of the component from the UNO PCB. Subtract the number from the USB (11mm),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
