# Fritzing sketch Servo_Light_Sensor (saved by Fritzing 0.9.10b)
breadboards: 1

parts:
  Part1 = Arduino Uno (Rev3)-TopMount
  AmbientLightSensor1 = AmbientLightSensor
  J1 = Basic Servo  # not connected
  J2 = Dagu DGServo 9g header connector (female) [package=THT]

nets:
  N1: Part1.A0, AmbientLightSensor1.SIG
  N2: Part1.D9_PWM, J2.Vcc
  GND: AmbientLightSensor1.GND, J2.gnd
  N3: AmbientLightSensor1.VCC, J2.pulse

custom parts:
  Arduino Uno (Rev3)-TopMount: Arduino Uno (Rev3) for Top PCB Mount. The PCB view of the Arduino Uno (Rev3) in Arduino Bin flipped upside down with the text flipped back so as to be readable. Other views haven't changed Protruding component position is outlined to provide indication of part contact. Number in component outline is mm of protrusion of the component from the UNO PCB. Subtract the number from the USB (11mm),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
