# Fritzing sketch Servo_Touch_Sensor (saved by Fritzing 0.9.10b)
breadboards: 1

parts:
  Part1 = Arduino Uno (Rev3)-TopMount
  J1 = Basic Servo
  DigitalTouchSensor1 = DigitalTouchSensor

nets:
  GND: Part1.A0, J1.gnd, DigitalTouchSensor1.Signal, DigitalTouchSensor1.GND
  N1: Part1.D7, J1.vcc
  5V: Part1.5V, J1.pulse, DigitalTouchSensor1.VIN

custom parts:
  Arduino Uno (Rev3)-TopMount: Arduino Uno (Rev3) for Top PCB Mount. The PCB view of the Arduino Uno (Rev3) in Arduino Bin flipped upside down with the text flipped back so as to be readable. Other views haven't changed Protruding component position is outlined to provide indication of part contact. Number in component outline is mm of protrusion of the component from the UNO PCB. Subtract the number from the USB (11mm),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
