# Fritzing sketch PIRMotionSensor (saved by Fritzing 0.9.10b)
breadboards: 1

parts:
  PIR1 = PIR sensor
  Part1 = Arduino Uno (Rev3)-TopMount
  NEOPIXEL1 = Neopixel Strip -- Black (30/m) [part_number=1376]

nets:
  VDD: PIR1.VDD, Part1.5V, NEOPIXEL1.+5V
  N1: PIR1.SIG, Part1.D2
  GND: PIR1.GND, Part1.GND, NEOPIXEL1.GND
  N2: Part1.D13/SCK, NEOPIXEL1.Din

custom parts:
  Arduino Uno (Rev3)-TopMount: Arduino Uno (Rev3) for Top PCB Mount. The PCB view of the Arduino Uno (Rev3) in Arduino Bin flipped upside down with the text flipped back so as to be readable. Other views haven't changed Protruding component position is outlined to provide indication of part contact. Number in component outline is mm of protrusion of the component from the UNO PCB. Subtract the number from the USB (11mm),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
  Neopixel Strip -- Black (30/m): These NeoPixel strips have 30 digitally-addressable pixel LEDs per meter and are very affordable and are only 12.5 mm wide, 10 mm if you remove the strip from the casing.
